// Logisim project Lab5_Continues.circ as structural Verilog
module modifying_the_alu (
  input  ctrl,
  input  [7:0] A,
  input  [1:0] au_selectors,
  input  [7:0] B,
  input  [2:0] lu_selectors,
  input  OE,
  output [7:0] au_dout,
  output [7:0] au_result,
  output cout,
  output lu_result
);

  AU au_1 (.CTRIL(ctrl), .A(A), .B(B), .selection_inputs(au_selectors), .out_5(cout), .result(au_result));
  LU lu_1 (.A(A), .B(B), .selectors(lu_selectors), .result(lu_result));
  assign au_dout = OE ? au_result : 8'bz;  // Controlled_Buffer controlled_buffer_1

  // Notes on the sheet:
  //   An 8-bit ALU
  //   selectors
  //   selectors
  //   Part 2.1: Modifying the ALU 
  //   8-bit result
  //   high or low
  //   for the 8-bit arithmetic result, which will be transported to the data bus in the CPU design. 
  //   The ALU must be modified to have Dout (connected by a controlled buffer and an OE input pin)
  //   AU Dout
  //   ALU Result
endmodule

module fullbitadder (
  input  A,
  input  B,
  input  Cin,
  output Sum,
  output Carry
);

  wire and_1_out, and_2_out, and_3_out, xor_1_out;

  xor xor_1 (xor_1_out, A, B);
  and and_1 (and_1_out, A, B);
  and and_2 (and_2_out, B, Cin);
  and and_3 (and_3_out, A, Cin);
  xor xor_2 (Sum, xor_1_out, Cin);
  or or_1 (Carry, and_1_out, and_2_out, and_3_out);

  // Notes on the sheet:
  //   A single-bit Full Adder
endmodule

module addsub8bit (
  input  Control,
  input  [7:0] A,
  input  [7:0] B,
  output [7:0] sum_or_difference,
  output discarded_overflow
);

  wire fullbitadder_1_carry, fullbitadder_2_carry, fullbitadder_3_carry, fullbitadder_4_carry,
       fullbitadder_5_carry, fullbitadder_6_carry, fullbitadder_7_carry, xor_1_out, xor_2_out, xor_3_out,
       xor_4_out, xor_5_out, xor_6_out, xor_7_out, xor_8_out;

  xor xor_1 (xor_1_out, Control, B[0]);
  xor xor_2 (xor_2_out, Control, B[1]);
  xor xor_3 (xor_3_out, Control, B[5]);
  xor xor_4 (xor_4_out, Control, B[6]);
  xor xor_5 (xor_5_out, Control, B[7]);
  xor xor_6 (xor_6_out, Control, B[2]);
  xor xor_7 (xor_7_out, Control, B[3]);
  xor xor_8 (xor_8_out, Control, B[4]);
  fullbitadder fullbitadder_1 (
    .A(A[0]), .B(xor_1_out), .Cin(Control), .Sum(sum_or_difference[0]), .Carry(fullbitadder_1_carry));
  fullbitadder fullbitadder_2 (
    .A(A[1]), .B(xor_2_out), .Cin(fullbitadder_1_carry), .Sum(sum_or_difference[1]),
    .Carry(fullbitadder_2_carry));
  fullbitadder fullbitadder_3 (
    .A(A[2]), .B(xor_6_out), .Cin(fullbitadder_2_carry), .Sum(sum_or_difference[2]),
    .Carry(fullbitadder_3_carry));
  fullbitadder fullbitadder_4 (
    .A(A[3]), .B(xor_7_out), .Cin(fullbitadder_3_carry), .Sum(sum_or_difference[3]),
    .Carry(fullbitadder_4_carry));
  fullbitadder fullbitadder_5 (
    .A(A[4]), .B(xor_8_out), .Cin(fullbitadder_4_carry), .Sum(sum_or_difference[4]),
    .Carry(fullbitadder_5_carry));
  fullbitadder fullbitadder_6 (
    .A(A[5]), .B(xor_3_out), .Cin(fullbitadder_5_carry), .Sum(sum_or_difference[5]),
    .Carry(fullbitadder_6_carry));
  fullbitadder fullbitadder_7 (
    .A(A[6]), .B(xor_4_out), .Cin(fullbitadder_6_carry), .Sum(sum_or_difference[6]),
    .Carry(fullbitadder_7_carry));
  fullbitadder fullbitadder_8 (
    .A(A[7]), .B(xor_5_out), .Cin(fullbitadder_7_carry), .Sum(sum_or_difference[7]),
    .Carry(discarded_overflow));

  // Notes on the sheet:
  //   8-bit Full Adder to Perform Subtraction
endmodule

module AU (
  input  CTRIL,
  input  [7:0] A,
  input  [7:0] B,
  input  [1:0] selection_inputs,
  output out_5,
  output [7:0] result
);

  wire [7:0] addsub8bit_1_sum_or_difference, divider_1_out, multiplier_1_out;

  Multiplier multiplier_1 (.a(A), .b(B), .out(multiplier_1_out));  // open: cin, cout
  Divider divider_1 (.a(A), .b(B), .out(divider_1_out));  // open: upper, rem
  addsub8bit addsub8bit_1 (
    .Control(CTRIL), .A(A), .B(B), .sum_or_difference(addsub8bit_1_sum_or_difference),
    .discarded_overflow(out_5));
  Multiplexer #(.select(2), .width(8)) multiplexer_1 (
    .in0(addsub8bit_1_sum_or_difference), .in1(multiplier_1_out), .in2(divider_1_out), .out(result),
    .sel(selection_inputs));  // open: in3

  // Notes on the sheet:
  //   An 8/bit ALU
  //   multiplier
  //   divider
endmodule

module LU (
  input  [7:0] A,
  input  [7:0] B,
  input  [2:0] selectors,
  output result
);

  wire comparator_1_eq, comparator_1_gt, comparator_1_lt, not_1_out, or_1_out, or_2_out;

  Comparator #(.mode("unsigned")) comparator_1 (
    .a(A), .b(B), .gt(comparator_1_gt), .eq(comparator_1_eq), .lt(comparator_1_lt));
  or or_1 (or_1_out, comparator_1_eq, comparator_1_gt);
  or or_2 (or_2_out, comparator_1_eq, comparator_1_lt);
  not not_1 (not_1_out, comparator_1_eq);
  Multiplexer #(.select(3)) multiplexer_1 (
    .in0(or_1_out), .in1(comparator_1_gt), .in2(comparator_1_eq), .in3(comparator_1_lt), .in4(or_2_out),
    .in5(not_1_out), .out(result), .sel(selectors));  // open: in6, in7

  // Notes on the sheet:
  //   Extended Logic Unit (LU)
  //   comparator
  //   =
  //   >=
  //   >
  //   <
  //   <=
  //   !=
  //   8 by 1 max
endmodule

module reg4bits (
  input  [3:0] DIN,
  input  WE,
  input  OE,
  input  Reset,
  input  Clock,
  output [3:0] dout,
  output [3:0] sd
);

  one_bit_memorycell one_bit_memorycell_1 (
    .WE(WE), .Din(DIN[3]), .clock(Clock), .OE(OE), .Reset(Reset), .Dout(dout[3]), .stored_data(sd[3]));
  one_bit_memorycell one_bit_memorycell_2 (
    .WE(WE), .Din(DIN[2]), .clock(Clock), .OE(OE), .Reset(Reset), .Dout(dout[2]), .stored_data(sd[2]));
  one_bit_memorycell one_bit_memorycell_3 (
    .WE(WE), .Din(DIN[1]), .clock(Clock), .OE(OE), .Reset(Reset), .Dout(dout[1]), .stored_data(sd[1]));
  one_bit_memorycell one_bit_memorycell_4 (
    .WE(WE), .Din(DIN[0]), .clock(Clock), .OE(OE), .Reset(Reset), .Dout(dout[0]), .stored_data(sd[0]));

  // Notes on the sheet:
  //   MAR_4_bit
  //   DOUT
  //   Part 2.2: Designing a 4-bit Register. 
  //   stored data
endmodule

module one_bit_memorycell (
  input  WE,
  input  Din,
  input  clock,
  input  OE,
  input  Reset,
  output Dout,
  output stored_data
);

  wire and_1_out, and_2_out, not_1_out, or_1_out;

  not not_1 (not_1_out, WE);
  and and_1 (and_1_out, stored_data, not_1_out);
  and and_2 (and_2_out, WE, Din);
  or or_1 (or_1_out, and_1_out, and_2_out);
  D_Flip_Flop d_ff_1 (.D(or_1_out), .clk(clock), .Q(stored_data), .reset(Reset));  // open: Qn, preset
  assign Dout = OE ? stored_data : 1'bz;  // Controlled_Buffer controlled_buffer_1

  // Notes on the sheet:
  //   Memory cell design using D flip-flops
  //   ctrled buffer
endmodule

module reg8bits (
  input  [7:0] Din,
  input  WE,
  input  OE,
  input  clock,
  input  Reset,
  output [7:0] dout,
  output [7:0] sd
);

  one_bit_memorycell one_bit_memorycell_1 (
    .WE(WE), .Din(Din[7]), .clock(clock), .OE(OE), .Reset(Reset), .Dout(dout[7]), .stored_data(sd[7]));
  one_bit_memorycell one_bit_memorycell_2 (
    .WE(WE), .Din(Din[6]), .clock(clock), .OE(OE), .Reset(Reset), .Dout(dout[6]), .stored_data(sd[6]));
  one_bit_memorycell one_bit_memorycell_3 (
    .WE(WE), .Din(Din[5]), .clock(clock), .OE(OE), .Reset(Reset), .Dout(dout[5]), .stored_data(sd[5]));
  one_bit_memorycell one_bit_memorycell_4 (
    .WE(WE), .Din(Din[4]), .clock(clock), .OE(OE), .Reset(Reset), .Dout(dout[4]), .stored_data(sd[4]));
  one_bit_memorycell one_bit_memorycell_5 (
    .WE(WE), .Din(Din[3]), .clock(clock), .OE(OE), .Reset(Reset), .Dout(dout[3]), .stored_data(sd[3]));
  one_bit_memorycell one_bit_memorycell_6 (
    .WE(WE), .Din(Din[2]), .clock(clock), .OE(OE), .Reset(Reset), .Dout(dout[2]), .stored_data(sd[2]));
  one_bit_memorycell one_bit_memorycell_7 (
    .WE(WE), .Din(Din[1]), .clock(clock), .OE(OE), .Reset(Reset), .Dout(dout[1]), .stored_data(sd[1]));
  one_bit_memorycell one_bit_memorycell_8 (
    .WE(WE), .Din(Din[0]), .clock(clock), .OE(OE), .Reset(Reset), .Dout(dout[0]), .stored_data(sd[0]));

  // Notes on the sheet:
  //   DOUT
  //   8-bit register
  //   Part 3: Designing an 8-bit Register
  //   stored data
endmodule

module six_bit_register (
  input  SW,
  input  [5:0] in_2,
  output Sout
);

  wire and_1_out, and_2_out, and_3_out, and_4_out, and_5_out, and_6_out, and_7_out, and_8_out, and_9_out,
       and_10_out, and_11_out, clock_1_out, d_ff_1_q, d_ff_2_q, d_ff_3_q, d_ff_4_q, d_ff_5_q, not_1_out,
       or_1_out, or_2_out, or_3_out, or_4_out, or_5_out;

  Clock clock_1 (.out(clock_1_out));
  not not_1 (not_1_out, SW);
  and and_1 (and_1_out, in_2[0], not_1_out);
  D_Flip_Flop d_ff_1 (.D(and_1_out), .clk(clock_1_out), .Q(d_ff_1_q));  // open: Qn, preset, reset
  and and_2 (and_2_out, not_1_out, in_2[1]);
  and and_3 (and_3_out, d_ff_1_q, SW);
  or or_1 (or_1_out, and_2_out, and_3_out);
  D_Flip_Flop d_ff_2 (.D(or_1_out), .clk(clock_1_out), .Q(d_ff_2_q));  // open: Qn, preset, reset
  and and_4 (and_4_out, not_1_out, in_2[2]);
  and and_5 (and_5_out, d_ff_2_q, SW);
  or or_2 (or_2_out, and_4_out, and_5_out);
  D_Flip_Flop d_ff_3 (.D(or_2_out), .clk(clock_1_out), .Q(d_ff_3_q));  // open: Qn, preset, reset
  and and_6 (and_6_out, not_1_out, in_2[3]);
  and and_7 (and_7_out, d_ff_3_q, SW);
  or or_3 (or_3_out, and_6_out, and_7_out);
  D_Flip_Flop d_ff_4 (.D(or_3_out), .clk(clock_1_out), .Q(d_ff_4_q));  // open: Qn, preset, reset
  and and_8 (and_8_out, not_1_out, in_2[4]);
  and and_9 (and_9_out, d_ff_4_q, SW);
  or or_4 (or_4_out, and_8_out, and_9_out);
  D_Flip_Flop d_ff_5 (.D(or_4_out), .clk(clock_1_out), .Q(d_ff_5_q));  // open: Qn, preset, reset
  and and_10 (and_10_out, not_1_out, in_2[5]);
  and and_11 (and_11_out, d_ff_5_q, SW);
  or or_5 (or_5_out, and_10_out, and_11_out);
  D_Flip_Flop d_ff_6 (.D(or_5_out), .clk(clock_1_out), .Q(Sout));  // open: Qn, preset, reset

  // Notes on the sheet:
  //   Task 1 
  //   Design a 6-bit Parallel-in / Serial-Out Register
endmodule

module cpu_datapath (
  input  [7:0] test_data,
  input  oe_testing_data,
  input  [3:0] in_3,
  input  ir_reset,
  input  in_5,
  input  reg_a_reset,
  input  [1:0] au_selectors,
  input  [2:0] lu_selectors,
  input  reg_b_reset,
  output [3:0] mar_content,
  output [3:0] counter_content,
  output [7:0] ir_content,
  output [7:0] mbr_content,
  output [7:0] reg_a_content,
  output [7:0] out_15,
  output [7:0] au_result,
  output out_17,
  output lu_result,
  output [7:0] reg_b_content,
  output [2:0] sc_content,
  output [31:0] out_21
);

  wire clock_1_out, Control_Unit_c0, Control_Unit_c1, Control_Unit_c2, Control_Unit_c3, Control_Unit_c4,
       Control_Unit_c5, Control_Unit_c6, Control_Unit_c7, Control_Unit_c8, Control_Unit_c9, Control_Unit_c10,
       Control_Unit_c11, Control_Unit_c12, Control_Unit_c13, Control_Unit_c14, Control_Unit_c15;
  wire [3:0] bitselector_2_out, controlled_buffer_1_out, decimal_decoder_1_dout_2, decimal_decoder_2_dout_2,
       decimal_decoder_4_dout_2, reg4bits_1_dout;
  wire [7:0] bit_extender_1_out, bit_extender_2_out, modifying_the_alu_1_au_dout, ram_1_dout, reg8bits_1_dout;
  wire [27:0] decimal_decoder_1_dout, decimal_decoder_2_dout, decimal_decoder_4_dout;
  wire [31:0] decimal_decoder_3_dout;

  Decimal_Decoder decimal_decoder_1 (.Din(reg_a_content), .Dout({decimal_decoder_1_dout_2, decimal_decoder_1_dout}));
  _7_Segment_Display u_7_segment_display_1 (
    .g(decimal_decoder_1_dout[15]), .f(decimal_decoder_1_dout[14]), .a(decimal_decoder_1_dout[13]),
    .b(decimal_decoder_1_dout[12]), .e(decimal_decoder_1_dout_2[3]), .d(decimal_decoder_1_dout_2[2]),
    .c(decimal_decoder_1_dout_2[1]), .dp(decimal_decoder_1_dout_2[0]));
  _7_Segment_Display u_7_segment_display_2 (
    .g(decimal_decoder_1_dout[11]), .f(decimal_decoder_1_dout[10]), .a(decimal_decoder_1_dout[9]),
    .b(decimal_decoder_1_dout[8]), .e(decimal_decoder_1_dout[27]), .d(decimal_decoder_1_dout[26]),
    .c(decimal_decoder_1_dout[25]), .dp(decimal_decoder_1_dout[24]));
  _7_Segment_Display u_7_segment_display_3 (
    .g(decimal_decoder_1_dout[7]), .f(decimal_decoder_1_dout[6]), .a(decimal_decoder_1_dout[5]),
    .b(decimal_decoder_1_dout[4]), .e(decimal_decoder_1_dout[23]), .d(decimal_decoder_1_dout[22]),
    .c(decimal_decoder_1_dout[21]), .dp(decimal_decoder_1_dout[20]));
  _7_Segment_Display u_7_segment_display_4 (
    .g(decimal_decoder_1_dout[3]), .f(decimal_decoder_1_dout[2]), .a(decimal_decoder_1_dout[1]),
    .b(decimal_decoder_1_dout[0]), .e(decimal_decoder_1_dout[19]), .d(decimal_decoder_1_dout[18]),
    .c(decimal_decoder_1_dout[17]), .dp(decimal_decoder_1_dout[16]));
  Clock clock_1 (.out(clock_1_out));
  Counter #(.max('h3), .width(4)) program_counter (
    .count(Control_Unit_c1), .clk(clock_1_out), .D(controlled_buffer_1_out), .Q(counter_content));  // open: clr, load, up, carry
  assign controlled_buffer_1_out = Control_Unit_c0 ? counter_content : 4'bz;  // Controlled_Buffer controlled_buffer_1
  _7_Segment_Display u_7_segment_display_5 (
    .g(decimal_decoder_2_dout[15]), .f(decimal_decoder_2_dout[14]), .a(decimal_decoder_2_dout[13]),
    .b(decimal_decoder_2_dout[12]), .e(decimal_decoder_2_dout_2[3]), .d(decimal_decoder_2_dout_2[2]),
    .c(decimal_decoder_2_dout_2[1]), .dp(decimal_decoder_2_dout_2[0]));
  assign bit_extender_1_out = {{4{1'b0}}, counter_content};  // Bit_Extender bit_extender_1
  reg8bits reg8bits_1 (
    .Din(modifying_the_alu_1_au_dout), .WE(Control_Unit_c7), .OE(Control_Unit_c8), .clock(clock_1_out),
    .Reset(ir_reset), .dout(reg8bits_1_dout), .sd(ir_content));
  reg8bits reg8bits_2 (
    .Din(modifying_the_alu_1_au_dout), .WE(Control_Unit_c12), .clock(clock_1_out), .Reset(reg_a_reset),
    .sd(reg_a_content));  // open: OE, dout
  modifying_the_alu modifying_the_alu_1 (
    .A(reg_a_content), .au_selectors(au_selectors), .B(reg_b_content), .lu_selectors(lu_selectors),
    .OE(Control_Unit_c11), .au_dout(modifying_the_alu_1_au_dout), .au_result(au_result), .cout(out_17),
    .lu_result(lu_result));  // open: ctrl
  reg8bits reg8bits_3 (
    .Din(modifying_the_alu_1_au_dout), .WE(Control_Unit_c13), .clock(clock_1_out), .Reset(reg_b_reset),
    .sd(reg_b_content));  // open: OE, dout
  Decimal_Decoder decimal_decoder_2 (.Din(reg_b_content), .Dout({decimal_decoder_2_dout_2, decimal_decoder_2_dout}));
  _7_Segment_Display u_7_segment_display_6 (
    .g(decimal_decoder_2_dout[11]), .f(decimal_decoder_2_dout[10]), .a(decimal_decoder_2_dout[9]),
    .b(decimal_decoder_2_dout[8]), .e(decimal_decoder_2_dout[27]), .d(decimal_decoder_2_dout[26]),
    .c(decimal_decoder_2_dout[25]), .dp(decimal_decoder_2_dout[24]));
  Decimal_Decoder decimal_decoder_3 (.Din(bit_extender_1_out), .Dout(decimal_decoder_3_dout));
  _7_Segment_Display u_7_segment_display_7 (
    .g(decimal_decoder_2_dout[7]), .f(decimal_decoder_2_dout[6]), .a(decimal_decoder_2_dout[5]),
    .b(decimal_decoder_2_dout[4]), .e(decimal_decoder_2_dout[23]), .d(decimal_decoder_2_dout[22]),
    .c(decimal_decoder_2_dout[21]), .dp(decimal_decoder_2_dout[20]));
  BitSelector #(.group(4)) bitselector_1 (.in(reg8bits_1_dout), .out(controlled_buffer_1_out), .sel(1'b0));
  _7_Segment_Display u_7_segment_display_8 (
    .g(decimal_decoder_2_dout[3]), .f(decimal_decoder_2_dout[2]), .a(decimal_decoder_2_dout[1]),
    .b(decimal_decoder_2_dout[0]), .e(decimal_decoder_2_dout[19]), .d(decimal_decoder_2_dout[18]),
    .c(decimal_decoder_2_dout[17]), .dp(decimal_decoder_2_dout[16]));
  _7_Segment_Display u_7_segment_display_9 (
    .g(decimal_decoder_3_dout[3]), .f(decimal_decoder_3_dout[2]), .a(decimal_decoder_3_dout[1]),
    .b(decimal_decoder_3_dout[0]), .e(decimal_decoder_3_dout[19]), .d(decimal_decoder_3_dout[18]),
    .c(decimal_decoder_3_dout[17]), .dp(decimal_decoder_3_dout[16]));
  LED D4 (.in(modifying_the_alu_1_au_dout[4]));
  LED D5 (.in(modifying_the_alu_1_au_dout[5]));
  LED D6 (.in(modifying_the_alu_1_au_dout[6]));
  LED D7 (.in(modifying_the_alu_1_au_dout[7]));
  assign modifying_the_alu_1_au_dout = oe_testing_data ? test_data : 8'bz;  // Controlled_Buffer controlled_buffer_2
  LED D3 (.in(modifying_the_alu_1_au_dout[3]));
  LED D2 (.in(modifying_the_alu_1_au_dout[2]));
  LED D1 (.in(modifying_the_alu_1_au_dout[1]));
  LED D0 (.in(modifying_the_alu_1_au_dout[0]));
  assign modifying_the_alu_1_au_dout = Control_Unit_c5 ? mbr_content : 8'bz;  // Controlled_Buffer controlled_buffer_3
  LED d_7 (.in(modifying_the_alu_1_au_dout[7]));
  reg4bits reg4bits_1 (
    .DIN(controlled_buffer_1_out), .WE(Control_Unit_c9), .OE(Control_Unit_c10), .Clock(clock_1_out),
    .dout(reg4bits_1_dout), .sd(mar_content));  // open: Reset
  reg8bits reg8bits_4 (
    .Din(modifying_the_alu_1_au_dout), .WE(Control_Unit_c4), .OE(Control_Unit_c6), .clock(clock_1_out),
    .dout(modifying_the_alu_1_au_dout), .sd(mbr_content));  // open: Reset
  reg8bits reg8bits_5 (
    .Din(modifying_the_alu_1_au_dout), .WE(Control_Unit_c15), .OE(Control_Unit_c14), .clock(clock_1_out),
    .dout(modifying_the_alu_1_au_dout), .sd(out_15));  // open: Reset
  LED d_5 (.in(modifying_the_alu_1_au_dout[5]));
  LED d_6 (.in(modifying_the_alu_1_au_dout[6]));
  _7_Segment_Display u_7_segment_display_10 (
    .g(decimal_decoder_4_dout[15]), .f(decimal_decoder_4_dout[14]), .a(decimal_decoder_4_dout[13]),
    .b(decimal_decoder_4_dout[12]), .e(decimal_decoder_4_dout_2[3]), .d(decimal_decoder_4_dout_2[2]),
    .c(decimal_decoder_4_dout_2[1]), .dp(decimal_decoder_4_dout_2[0]));
  LED d_4 (.in(modifying_the_alu_1_au_dout[4]));
  Decimal_Decoder decimal_decoder_4 (.Din(out_15), .Dout({decimal_decoder_4_dout_2, decimal_decoder_4_dout}));
  _7_Segment_Display u_7_segment_display_11 (
    .g(decimal_decoder_4_dout[11]), .f(decimal_decoder_4_dout[10]), .a(decimal_decoder_4_dout[9]),
    .b(decimal_decoder_4_dout[8]), .e(decimal_decoder_4_dout[27]), .d(decimal_decoder_4_dout[26]),
    .c(decimal_decoder_4_dout[25]), .dp(decimal_decoder_4_dout[24]));
  _7_Segment_Display u_7_segment_display_12 (
    .g(decimal_decoder_4_dout[7]), .f(decimal_decoder_4_dout[6]), .a(decimal_decoder_4_dout[5]),
    .b(decimal_decoder_4_dout[4]), .e(decimal_decoder_4_dout[23]), .d(decimal_decoder_4_dout[22]),
    .c(decimal_decoder_4_dout[21]), .dp(decimal_decoder_4_dout[20]));
  _7_Segment_Display u_7_segment_display_13 (
    .g(decimal_decoder_4_dout[3]), .f(decimal_decoder_4_dout[2]), .a(decimal_decoder_4_dout[1]),
    .b(decimal_decoder_4_dout[0]), .e(decimal_decoder_4_dout[19]), .d(decimal_decoder_4_dout[18]),
    .c(decimal_decoder_4_dout[17]), .dp(decimal_decoder_4_dout[16]));
  LED d_3 (.in(modifying_the_alu_1_au_dout[3]));
  assign reg4bits_1_dout = in_5 ? in_3 : 4'bz;  // Controlled_Buffer controlled_buffer_4
  LED d_2 (.in(modifying_the_alu_1_au_dout[2]));
  LED d_1 (.in(modifying_the_alu_1_au_dout[1]));
  LED d_0 (.in(modifying_the_alu_1_au_dout[0]));
  RAM #(.addrWidth(4), .enables("line")) ram_1 (
    .addr(reg4bits_1_dout), .we(Control_Unit_c2), .clk(clock_1_out), .din(modifying_the_alu_1_au_dout),
    .dout(ram_1_dout));
  assign modifying_the_alu_1_au_dout = Control_Unit_c3 ? ram_1_dout : 8'bz;  // Controlled_Buffer controlled_buffer_5
  Counter #(.max('h5), .width(3)) Step_Counter (
    .clk(clock_1_out), .Q(sc_content));  // open: clr, load, up, count, D, carry
  BitSelector #(.group(4)) bitselector_2 (.in(ir_content), .out(bitselector_2_out), .sel(1'b1));
  assign bit_extender_2_out = {{5{1'b0}}, sc_content};  // Bit_Extender bit_extender_2
  Decimal_Decoder decimal_decoder_5 (.Din(bit_extender_2_out), .Dout(out_21));
  _7_Segment_Display u_7_segment_display_14 (
    .g(out_21[3]), .f(out_21[2]), .a(out_21[1]), .b(out_21[0]), .e(out_21[19]), .d(out_21[18]),
    .c(out_21[17]), .dp(out_21[16]));
  CU Control_Unit (
    .OPC3(bitselector_2_out[3]), .OPC2(bitselector_2_out[2]), .OPC1(bitselector_2_out[1]),
    .OPC0(bitselector_2_out[0]), .SC2(sc_content[2]), .SC1(sc_content[1]), .SC0(sc_content[0]),
    .C0(Control_Unit_c0), .C1(Control_Unit_c1), .C2(Control_Unit_c2), .C3(Control_Unit_c3),
    .C4(Control_Unit_c4), .C5(Control_Unit_c5), .C6(Control_Unit_c6), .C7(Control_Unit_c7),
    .C8(Control_Unit_c8), .C9(Control_Unit_c9), .C10(Control_Unit_c10), .C11(Control_Unit_c11),
    .C12(Control_Unit_c12), .C13(Control_Unit_c13), .C14(Control_Unit_c14), .C15(Control_Unit_c15));

  // Notes on the sheet:
  //   clock
  //   Instruction Register (IR)
  //   register A
  //   ALU
  //   register B
  //   controlled buffer
  //   Internal Address Bus (4 bits) 
  //   Internal Address Bus
  //   oe
  //   Updated Datapath with Program Counter and 7-segment display features 
  //   Part 1: Designing a Program Counter (PC) 
  //   Memory Buffer Register (MBR)
  //   Memory Address Register (MAR)
  //    Output Register (OR)
  //   controlled buffer
  //   output_reg_content
  //   External Address Bus
  //   External Address Bus
  //   oe test
  //   RAM
endmodule

module Decimal_Decoder (
  input  [7:0] Din,
  output [31:0] Dout
);

  ROM #(.dataWidth(32)) Decimal_Decoder (
    .addr(Din),
    .data({Dout[31:28], Dout[15:12], Dout[27:24], Dout[11:8], Dout[23:20], Dout[7:4], Dout[19:16], Dout[3:0]}));

  // Notes on the sheet:
  //   contents of Decimal_Decoder (hex, n*v repeats v):
  //   e7 21 cb 6b 2d 6e ee 23 ef 2f 21e7 2121 21cb 216b 212d 216e 21ee 2123 21ef 212f cbe7 cb21 cbcb cb6b
  //   cb2d cb6e cbee cb23 cbef cb2f 6be7 6b21 6bcb 6b6b 6b2d 6b6e 6bee 6b23 6bef 6b2f 2de7 2d21 2dcb 2d6b
  //   2d2d 2d6e 2dee 2d23 2def 2d2f 6ee7 6e21 6ecb 6e6b 6e2d 6e6e 6eee 6e23 6eef 6e2f eee7 ee21 eecb ee6b
  //   ee2d ee6e eeee ee23 eeef ee2f 23e7 2321 23cb 236b 232d 236e 23ee 2323 23ef 232f efe7 ef21 efcb ef6b
  //   ef2d ef6e efee ef23 efef ef2f 2fe7 2f21 2fcb 2f6b 2f2d 2f6e 2fee 2f23 2fef 2f2f 21e7e7 21e721 21e7cb
  //   21e76b 21e72d 21e76e 21e7ee 21e723 21e7ef 21e72f 2121e7 212121 2121cb 21216b 21212d 21216e 2121ee
  //   212123 2121ef 21212f 21cbe7 21cb21 21cbcb 21cb6b 21cb2d 21cb6e 21cbee 21cb23 21cbef 21cb2f 216be7
  //   216b21 216bcb 216b6b 216b2d 216b6e 216bee 216b23 216bef 216b2f 212de7 212d21 212dcb 212d6b 212d2d
  //   212d6e 212dee 212d23 212def 212d2f 216ee7 216e21 216ecb 216e6b 216e2d 216e6e 216eee 216e23 216eef
  //   216e2f 21eee7 21ee21 21eecb 21ee6b 21ee2d 21ee6e 21eeee 21ee23 21eeef 21ee2f 2123e7 212321 2123cb
  //   21236b 21232d 21236e 2123ee 212323 2123ef 21232f 21efe7 21ef21 21efcb 21ef6b 21ef2d 21ef6e 21efee
  //   21ef23 21efef 21ef2f 212fe7 212f21 212fcb 212f6b 212f2d 212f6e 212fee 212f23 212fef 212f2f cbe7e7
  //   cbe721 cbe7cb cbe76b cbe72d cbe76e cbe7ee cbe723 cbe7ef cbe72f cb21e7 cb2121 cb21cb cb216b cb212d
  //   cb216e cb21ee cb2123 cb21ef cb212f cbcbe7 cbcb21 cbcbcb cbcb6b cbcb2d cbcb6e cbcbee cbcb23 cbcbef
  //   cbcb2f cb6be7 cb6b21 cb6bcb cb6b6b cb6b2d cb6b6e cb6bee cb6b23 cb6bef cb6b2f cb2de7 cb2d21 cb2dcb
  //   cb2d6b cb2d2d cb2d6e cb2dee cb2d23 cb2def cb2d2f cb6ee7 cb6e21 cb6ecb cb6e6b cb6e2d cb6e6e
  //   Part 2: Designing a Decimal Decoder for 7 Segment Display
  //   Decimal Decoder using ROM
endmodule

module backupcpu (
  input  counter_oe,
  input  [7:0] test_data,
  input  count_enable,
  input  we,
  input  oe_testing_data,
  input  oe,
  input  intern_oe,
  input  we_2,
  input  we_3,
  input  oe_2,
  input  [3:0] in_11,
  input  oe_3,
  input  ir_reset,
  input  write_enable,
  input  in_15,
  input  we_4,
  input  reg_a_reset,
  input  in_18,
  input  [1:0] au_selectors,
  input  we_5,
  input  o_e,
  input  oe_4,
  input  [2:0] lu_selectors,
  input  w_e,
  input  reg_b_reset,
  output [3:0] mar_content,
  output [3:0] counter_content,
  output [7:0] ir_content,
  output [7:0] mbr_content,
  output [7:0] reg_a_content,
  output [7:0] out_31,
  output [7:0] au_result,
  output out_33,
  output lu_result,
  output [7:0] reg_b_content
);

  wire clock_1_out;
  wire [3:0] controlled_buffer_1_out, decimal_decoder_1_dout_2, decimal_decoder_2_dout_2,
       decimal_decoder_4_dout_2, reg4bits_1_dout;
  wire [7:0] bit_extender_1_out, modifying_the_alu_1_au_dout, ram_1_dout, reg8bits_1_dout;
  wire [27:0] decimal_decoder_1_dout, decimal_decoder_2_dout, decimal_decoder_4_dout;
  wire [31:0] decimal_decoder_3_dout;

  _7_Segment_Display u_7_segment_display_1 (
    .g(decimal_decoder_1_dout[15]), .f(decimal_decoder_1_dout[14]), .a(decimal_decoder_1_dout[13]),
    .b(decimal_decoder_1_dout[12]), .e(decimal_decoder_1_dout_2[3]), .d(decimal_decoder_1_dout_2[2]),
    .c(decimal_decoder_1_dout_2[1]), .dp(decimal_decoder_1_dout_2[0]));
  Decimal_Decoder decimal_decoder_1 (.Din(reg_a_content), .Dout({decimal_decoder_1_dout_2, decimal_decoder_1_dout}));
  _7_Segment_Display u_7_segment_display_2 (
    .g(decimal_decoder_1_dout[11]), .f(decimal_decoder_1_dout[10]), .a(decimal_decoder_1_dout[9]),
    .b(decimal_decoder_1_dout[8]), .e(decimal_decoder_1_dout[27]), .d(decimal_decoder_1_dout[26]),
    .c(decimal_decoder_1_dout[25]), .dp(decimal_decoder_1_dout[24]));
  _7_Segment_Display u_7_segment_display_3 (
    .g(decimal_decoder_1_dout[7]), .f(decimal_decoder_1_dout[6]), .a(decimal_decoder_1_dout[5]),
    .b(decimal_decoder_1_dout[4]), .e(decimal_decoder_1_dout[23]), .d(decimal_decoder_1_dout[22]),
    .c(decimal_decoder_1_dout[21]), .dp(decimal_decoder_1_dout[20]));
  _7_Segment_Display u_7_segment_display_4 (
    .g(decimal_decoder_1_dout[3]), .f(decimal_decoder_1_dout[2]), .a(decimal_decoder_1_dout[1]),
    .b(decimal_decoder_1_dout[0]), .e(decimal_decoder_1_dout[19]), .d(decimal_decoder_1_dout[18]),
    .c(decimal_decoder_1_dout[17]), .dp(decimal_decoder_1_dout[16]));
  Clock clock_1 (.out(clock_1_out));
  Counter #(.max('h3), .width(4)) program_counter (
    .count(count_enable), .clk(clock_1_out), .D(controlled_buffer_1_out), .Q(counter_content));  // open: clr, load, up, carry
  assign controlled_buffer_1_out = counter_oe ? counter_content : 4'bz;  // Controlled_Buffer controlled_buffer_1
  Decimal_Decoder decimal_decoder_2 (.Din(reg_b_content), .Dout({decimal_decoder_2_dout_2, decimal_decoder_2_dout}));
  _7_Segment_Display u_7_segment_display_5 (
    .g(decimal_decoder_2_dout[15]), .f(decimal_decoder_2_dout[14]), .a(decimal_decoder_2_dout[13]),
    .b(decimal_decoder_2_dout[12]), .e(decimal_decoder_2_dout_2[3]), .d(decimal_decoder_2_dout_2[2]),
    .c(decimal_decoder_2_dout_2[1]), .dp(decimal_decoder_2_dout_2[0]));
  assign bit_extender_1_out = {{4{1'b0}}, counter_content};  // Bit_Extender bit_extender_1
  reg8bits reg8bits_1 (
    .Din(modifying_the_alu_1_au_dout), .WE(we_3), .OE(oe_3), .clock(clock_1_out), .Reset(ir_reset),
    .dout(reg8bits_1_dout), .sd(ir_content));
  reg8bits reg8bits_2 (
    .Din(modifying_the_alu_1_au_dout), .WE(we_4), .clock(clock_1_out), .Reset(reg_a_reset), .sd(reg_a_content));  // open: OE, dout
  modifying_the_alu modifying_the_alu_1 (
    .A(reg_a_content), .au_selectors(au_selectors), .B(reg_b_content), .lu_selectors(lu_selectors),
    .OE(oe_4), .au_dout(modifying_the_alu_1_au_dout), .au_result(au_result), .cout(out_33),
    .lu_result(lu_result));  // open: ctrl
  reg8bits reg8bits_3 (
    .Din(modifying_the_alu_1_au_dout), .WE(w_e), .clock(clock_1_out), .Reset(reg_b_reset), .sd(reg_b_content));  // open: OE, dout
  _7_Segment_Display u_7_segment_display_6 (
    .g(decimal_decoder_2_dout[11]), .f(decimal_decoder_2_dout[10]), .a(decimal_decoder_2_dout[9]),
    .b(decimal_decoder_2_dout[8]), .e(decimal_decoder_2_dout[27]), .d(decimal_decoder_2_dout[26]),
    .c(decimal_decoder_2_dout[25]), .dp(decimal_decoder_2_dout[24]));
  Decimal_Decoder decimal_decoder_3 (.Din(bit_extender_1_out), .Dout(decimal_decoder_3_dout));
  _7_Segment_Display u_7_segment_display_7 (
    .g(decimal_decoder_2_dout[7]), .f(decimal_decoder_2_dout[6]), .a(decimal_decoder_2_dout[5]),
    .b(decimal_decoder_2_dout[4]), .e(decimal_decoder_2_dout[23]), .d(decimal_decoder_2_dout[22]),
    .c(decimal_decoder_2_dout[21]), .dp(decimal_decoder_2_dout[20]));
  BitSelector #(.group(4)) bitselector_1 (.in(reg8bits_1_dout), .out(controlled_buffer_1_out), .sel(1'b0));
  _7_Segment_Display u_7_segment_display_8 (
    .g(decimal_decoder_2_dout[3]), .f(decimal_decoder_2_dout[2]), .a(decimal_decoder_2_dout[1]),
    .b(decimal_decoder_2_dout[0]), .e(decimal_decoder_2_dout[19]), .d(decimal_decoder_2_dout[18]),
    .c(decimal_decoder_2_dout[17]), .dp(decimal_decoder_2_dout[16]));
  _7_Segment_Display u_7_segment_display_9 (
    .g(decimal_decoder_3_dout[3]), .f(decimal_decoder_3_dout[2]), .a(decimal_decoder_3_dout[1]),
    .b(decimal_decoder_3_dout[0]), .e(decimal_decoder_3_dout[19]), .d(decimal_decoder_3_dout[18]),
    .c(decimal_decoder_3_dout[17]), .dp(decimal_decoder_3_dout[16]));
  LED D7 (.in(modifying_the_alu_1_au_dout[7]));
  LED D4 (.in(modifying_the_alu_1_au_dout[4]));
  LED D5 (.in(modifying_the_alu_1_au_dout[5]));
  LED D6 (.in(modifying_the_alu_1_au_dout[6]));
  assign modifying_the_alu_1_au_dout = oe_testing_data ? test_data : 8'bz;  // Controlled_Buffer controlled_buffer_2
  LED D3 (.in(modifying_the_alu_1_au_dout[3]));
  LED D2 (.in(modifying_the_alu_1_au_dout[2]));
  LED D1 (.in(modifying_the_alu_1_au_dout[1]));
  LED D0 (.in(modifying_the_alu_1_au_dout[0]));
  assign modifying_the_alu_1_au_dout = intern_oe ? mbr_content : 8'bz;  // Controlled_Buffer controlled_buffer_3
  reg8bits reg8bits_4 (
    .Din(modifying_the_alu_1_au_dout), .WE(we_2), .OE(oe_2), .clock(clock_1_out),
    .dout(modifying_the_alu_1_au_dout), .sd(mbr_content));  // open: Reset
  LED d_7 (.in(modifying_the_alu_1_au_dout[7]));
  reg4bits reg4bits_1 (
    .DIN(controlled_buffer_1_out), .WE(we), .OE(oe), .Clock(clock_1_out), .dout(reg4bits_1_dout),
    .sd(mar_content));  // open: Reset
  reg8bits reg8bits_5 (
    .Din(modifying_the_alu_1_au_dout), .WE(we_5), .OE(o_e), .clock(clock_1_out),
    .dout(modifying_the_alu_1_au_dout), .sd(out_31));  // open: Reset
  LED d_4 (.in(modifying_the_alu_1_au_dout[4]));
  LED d_5 (.in(modifying_the_alu_1_au_dout[5]));
  LED d_6 (.in(modifying_the_alu_1_au_dout[6]));
  _7_Segment_Display u_7_segment_display_10 (
    .g(decimal_decoder_4_dout[15]), .f(decimal_decoder_4_dout[14]), .a(decimal_decoder_4_dout[13]),
    .b(decimal_decoder_4_dout[12]), .e(decimal_decoder_4_dout_2[3]), .d(decimal_decoder_4_dout_2[2]),
    .c(decimal_decoder_4_dout_2[1]), .dp(decimal_decoder_4_dout_2[0]));
  Decimal_Decoder decimal_decoder_4 (.Din(out_31), .Dout({decimal_decoder_4_dout_2, decimal_decoder_4_dout}));
  _7_Segment_Display u_7_segment_display_11 (
    .g(decimal_decoder_4_dout[11]), .f(decimal_decoder_4_dout[10]), .a(decimal_decoder_4_dout[9]),
    .b(decimal_decoder_4_dout[8]), .e(decimal_decoder_4_dout[27]), .d(decimal_decoder_4_dout[26]),
    .c(decimal_decoder_4_dout[25]), .dp(decimal_decoder_4_dout[24]));
  _7_Segment_Display u_7_segment_display_12 (
    .g(decimal_decoder_4_dout[7]), .f(decimal_decoder_4_dout[6]), .a(decimal_decoder_4_dout[5]),
    .b(decimal_decoder_4_dout[4]), .e(decimal_decoder_4_dout[23]), .d(decimal_decoder_4_dout[22]),
    .c(decimal_decoder_4_dout[21]), .dp(decimal_decoder_4_dout[20]));
  _7_Segment_Display u_7_segment_display_13 (
    .g(decimal_decoder_4_dout[3]), .f(decimal_decoder_4_dout[2]), .a(decimal_decoder_4_dout[1]),
    .b(decimal_decoder_4_dout[0]), .e(decimal_decoder_4_dout[19]), .d(decimal_decoder_4_dout[18]),
    .c(decimal_decoder_4_dout[17]), .dp(decimal_decoder_4_dout[16]));
  LED d_3 (.in(modifying_the_alu_1_au_dout[3]));
  LED d_2 (.in(modifying_the_alu_1_au_dout[2]));
  assign reg4bits_1_dout = in_15 ? in_11 : 4'bz;  // Controlled_Buffer controlled_buffer_4
  LED d_1 (.in(modifying_the_alu_1_au_dout[1]));
  LED d_0 (.in(modifying_the_alu_1_au_dout[0]));
  assign modifying_the_alu_1_au_dout = in_18 ? ram_1_dout : 8'bz;  // Controlled_Buffer controlled_buffer_5
  RAM #(.addrWidth(4), .enables("line")) ram_1 (
    .addr(reg4bits_1_dout), .we(write_enable), .clk(clock_1_out), .din(modifying_the_alu_1_au_dout),
    .dout(ram_1_dout));

  // Notes on the sheet:
  //   clock
  //   Instruction Register (IR)
  //   register A
  //   ALU
  //   register B
  //   controlled buffer
  //   Internal Address Bus (4 bits) 
  //   Internal Address Bus
  //   Part 1: Designing a Program Counter (PC) 
  //   Updated Datapath with Program Counter and 7-segment display features 
  //   Memory Buffer Register (MBR)
  //    Output Register (OR)
  //   Memory Address Register (MAR)
  //   controlled buffer
  //   output_reg_content
  //   External Address Bus
  //   External Address Bus
  //   oe test
  //   oe
  //   RAM
endmodule

module CU (
  input  OPC3,
  input  OPC2,
  input  OPC1,
  input  OPC0,
  input  SC2,
  input  SC1,
  input  SC0,
  output C0,
  output C1,
  output C2,
  output C3,
  output C4,
  output C5,
  output C6,
  output C7,
  output C8,
  output C9,
  output C10,
  output C11,
  output C12,
  output C13,
  output C14,
  output C15
);

  wire and_4_out, and_5_out, and_6_out, and_7_out, and_8_out, and_9_out, and_10_out, and_13_out, and_14_out,
       and_15_out, and_16_out, and_17_out, and_18_out, and_19_out, and_20_out, not_1_out, not_2_out,
       not_3_out, not_4_out, not_5_out;

  not not_1 (not_1_out, OPC1);
  not not_2 (not_2_out, OPC0);
  not not_3 (not_3_out, SC2);
  not not_4 (not_4_out, SC1);
  not not_5 (not_5_out, SC0);
  and and_1 (C0, not_3_out, not_4_out, not_5_out);
  and and_2 (C1, not_3_out, not_4_out, SC0);
  and and_3 (C2, OPC1, OPC0, SC2, not_4_out, not_5_out);
  and and_4 (and_4_out, not_3_out, not_4_out, SC0);
  and and_5 (and_5_out, not_1_out, SC2, not_4_out, not_5_out);
  and and_6 (and_6_out, not_3_out, not_4_out, SC0);
  and and_7 (and_7_out, not_1_out, SC2, not_4_out, not_5_out);
  and and_8 (and_8_out, OPC1, OPC0, not_3_out, SC0);
  and and_9 (and_9_out, not_3_out, SC1, not_5_out);
  and and_10 (and_10_out, not_1_out, SC2, not_4_out, SC0);
  and and_11 (C6, OPC1, OPC0, SC2, not_4_out, not_5_out);
  and and_12 (C7, not_3_out, SC1, not_5_out);
  and and_13 (and_13_out, not_1_out, not_3_out, SC1, SC0);
  and and_14 (and_14_out, OPC0, not_3_out, SC1, SC0);
  and and_15 (and_15_out, not_3_out, not_4_out, not_5_out);
  and and_16 (and_16_out, not_1_out, not_3_out, SC1, SC0);
  and and_17 (and_17_out, OPC0, not_3_out, SC1, SC0);
  and and_18 (and_18_out, not_3_out, not_4_out, SC0);
  and and_19 (and_19_out, not_1_out, SC2, not_4_out, not_5_out);
  and and_20 (and_20_out, OPC0, SC2, not_4_out, not_5_out);
  and and_21 (C11, OPC1, not_2_out, not_3_out, SC1, SC0);
  and and_22 (C12, not_1_out, not_2_out, SC2, not_4_out, SC0);
  and and_23 (C13, not_1_out, OPC0, SC2, not_4_out, SC0);
  and and_24 (C14, OPC1, OPC0, not_3_out, SC1, SC0);
  and and_25 (C15, OPC1, not_2_out, not_3_out, SC1, SC0);
  or or_1 (C3, and_4_out, and_5_out);
  or or_2 (C4, and_6_out, and_7_out, and_8_out);
  or or_3 (C5, and_9_out, and_10_out);
  or or_4 (C8, and_13_out, and_14_out);
  or or_5 (C9, and_15_out, and_16_out, and_17_out);
  or or_6 (C10, and_18_out, and_19_out, and_20_out);

  // Notes on the sheet:
  //   Part 7: Designing the Control Unit
  //   Control Unit
endmodule

module backupcpu2 (
  input  counter_oe,
  input  [7:0] test_data,
  input  count_enable,
  input  we,
  input  oe_testing_data,
  input  oe,
  input  intern_oe,
  input  we_2,
  input  we_3,
  input  oe_2,
  input  [3:0] in_11,
  input  oe_3,
  input  ir_reset,
  input  write_enable,
  input  in_15,
  input  we_4,
  input  reg_a_reset,
  input  in_18,
  input  [1:0] au_selectors,
  input  we_5,
  input  o_e,
  input  oe_4,
  input  [2:0] lu_selectors,
  input  w_e,
  input  reg_b_reset,
  output [3:0] mar_content,
  output [3:0] counter_content,
  output [7:0] ir_content,
  output [7:0] mbr_content,
  output [7:0] reg_a_content,
  output [7:0] out_31,
  output [7:0] au_result,
  output out_33,
  output lu_result,
  output [7:0] reg_b_content,
  output [2:0] sc_content,
  output [31:0] out_37
);

  wire clock_1_out;
  wire [3:0] bitselector_2_out, controlled_buffer_1_out, decimal_decoder_1_dout_2, decimal_decoder_2_dout_2,
       decimal_decoder_4_dout_2, reg4bits_1_dout;
  wire [7:0] bit_extender_1_out, bit_extender_2_out, modifying_the_alu_1_au_dout, ram_1_dout, reg8bits_1_dout;
  wire [27:0] decimal_decoder_1_dout, decimal_decoder_2_dout, decimal_decoder_4_dout;
  wire [31:0] decimal_decoder_3_dout;

  Decimal_Decoder decimal_decoder_1 (.Din(reg_a_content), .Dout({decimal_decoder_1_dout_2, decimal_decoder_1_dout}));
  _7_Segment_Display u_7_segment_display_1 (
    .g(decimal_decoder_1_dout[15]), .f(decimal_decoder_1_dout[14]), .a(decimal_decoder_1_dout[13]),
    .b(decimal_decoder_1_dout[12]), .e(decimal_decoder_1_dout_2[3]), .d(decimal_decoder_1_dout_2[2]),
    .c(decimal_decoder_1_dout_2[1]), .dp(decimal_decoder_1_dout_2[0]));
  _7_Segment_Display u_7_segment_display_2 (
    .g(decimal_decoder_1_dout[11]), .f(decimal_decoder_1_dout[10]), .a(decimal_decoder_1_dout[9]),
    .b(decimal_decoder_1_dout[8]), .e(decimal_decoder_1_dout[27]), .d(decimal_decoder_1_dout[26]),
    .c(decimal_decoder_1_dout[25]), .dp(decimal_decoder_1_dout[24]));
  _7_Segment_Display u_7_segment_display_3 (
    .g(decimal_decoder_1_dout[7]), .f(decimal_decoder_1_dout[6]), .a(decimal_decoder_1_dout[5]),
    .b(decimal_decoder_1_dout[4]), .e(decimal_decoder_1_dout[23]), .d(decimal_decoder_1_dout[22]),
    .c(decimal_decoder_1_dout[21]), .dp(decimal_decoder_1_dout[20]));
  _7_Segment_Display u_7_segment_display_4 (
    .g(decimal_decoder_1_dout[3]), .f(decimal_decoder_1_dout[2]), .a(decimal_decoder_1_dout[1]),
    .b(decimal_decoder_1_dout[0]), .e(decimal_decoder_1_dout[19]), .d(decimal_decoder_1_dout[18]),
    .c(decimal_decoder_1_dout[17]), .dp(decimal_decoder_1_dout[16]));
  Clock clock_1 (.out(clock_1_out));
  Counter #(.max('h3), .width(4)) program_counter (
    .count(count_enable), .clk(clock_1_out), .D(controlled_buffer_1_out), .Q(counter_content));  // open: clr, load, up, carry
  assign controlled_buffer_1_out = counter_oe ? counter_content : 4'bz;  // Controlled_Buffer controlled_buffer_1
  _7_Segment_Display u_7_segment_display_5 (
    .g(decimal_decoder_2_dout[15]), .f(decimal_decoder_2_dout[14]), .a(decimal_decoder_2_dout[13]),
    .b(decimal_decoder_2_dout[12]), .e(decimal_decoder_2_dout_2[3]), .d(decimal_decoder_2_dout_2[2]),
    .c(decimal_decoder_2_dout_2[1]), .dp(decimal_decoder_2_dout_2[0]));
  assign bit_extender_1_out = {{4{1'b0}}, counter_content};  // Bit_Extender bit_extender_1
  reg8bits reg8bits_1 (
    .Din(modifying_the_alu_1_au_dout), .WE(we_3), .OE(oe_3), .clock(clock_1_out), .Reset(ir_reset),
    .dout(reg8bits_1_dout), .sd(ir_content));
  reg8bits reg8bits_2 (
    .Din(modifying_the_alu_1_au_dout), .WE(we_4), .clock(clock_1_out), .Reset(reg_a_reset), .sd(reg_a_content));  // open: OE, dout
  modifying_the_alu modifying_the_alu_1 (
    .A(reg_a_content), .au_selectors(au_selectors), .B(reg_b_content), .lu_selectors(lu_selectors),
    .OE(oe_4), .au_dout(modifying_the_alu_1_au_dout), .au_result(au_result), .cout(out_33),
    .lu_result(lu_result));  // open: ctrl
  reg8bits reg8bits_3 (
    .Din(modifying_the_alu_1_au_dout), .WE(w_e), .clock(clock_1_out), .Reset(reg_b_reset), .sd(reg_b_content));  // open: OE, dout
  Decimal_Decoder decimal_decoder_2 (.Din(reg_b_content), .Dout({decimal_decoder_2_dout_2, decimal_decoder_2_dout}));
  _7_Segment_Display u_7_segment_display_6 (
    .g(decimal_decoder_2_dout[11]), .f(decimal_decoder_2_dout[10]), .a(decimal_decoder_2_dout[9]),
    .b(decimal_decoder_2_dout[8]), .e(decimal_decoder_2_dout[27]), .d(decimal_decoder_2_dout[26]),
    .c(decimal_decoder_2_dout[25]), .dp(decimal_decoder_2_dout[24]));
  Decimal_Decoder decimal_decoder_3 (.Din(bit_extender_1_out), .Dout(decimal_decoder_3_dout));
  _7_Segment_Display u_7_segment_display_7 (
    .g(decimal_decoder_2_dout[7]), .f(decimal_decoder_2_dout[6]), .a(decimal_decoder_2_dout[5]),
    .b(decimal_decoder_2_dout[4]), .e(decimal_decoder_2_dout[23]), .d(decimal_decoder_2_dout[22]),
    .c(decimal_decoder_2_dout[21]), .dp(decimal_decoder_2_dout[20]));
  BitSelector #(.group(4)) bitselector_1 (.in(reg8bits_1_dout), .out(controlled_buffer_1_out), .sel(1'b0));
  _7_Segment_Display u_7_segment_display_8 (
    .g(decimal_decoder_2_dout[3]), .f(decimal_decoder_2_dout[2]), .a(decimal_decoder_2_dout[1]),
    .b(decimal_decoder_2_dout[0]), .e(decimal_decoder_2_dout[19]), .d(decimal_decoder_2_dout[18]),
    .c(decimal_decoder_2_dout[17]), .dp(decimal_decoder_2_dout[16]));
  _7_Segment_Display u_7_segment_display_9 (
    .g(decimal_decoder_3_dout[3]), .f(decimal_decoder_3_dout[2]), .a(decimal_decoder_3_dout[1]),
    .b(decimal_decoder_3_dout[0]), .e(decimal_decoder_3_dout[19]), .d(decimal_decoder_3_dout[18]),
    .c(decimal_decoder_3_dout[17]), .dp(decimal_decoder_3_dout[16]));
  LED D4 (.in(modifying_the_alu_1_au_dout[4]));
  LED D5 (.in(modifying_the_alu_1_au_dout[5]));
  LED D6 (.in(modifying_the_alu_1_au_dout[6]));
  LED D7 (.in(modifying_the_alu_1_au_dout[7]));
  assign modifying_the_alu_1_au_dout = oe_testing_data ? test_data : 8'bz;  // Controlled_Buffer controlled_buffer_2
  LED D3 (.in(modifying_the_alu_1_au_dout[3]));
  LED D2 (.in(modifying_the_alu_1_au_dout[2]));
  LED D1 (.in(modifying_the_alu_1_au_dout[1]));
  LED D0 (.in(modifying_the_alu_1_au_dout[0]));
  assign modifying_the_alu_1_au_dout = intern_oe ? mbr_content : 8'bz;  // Controlled_Buffer controlled_buffer_3
  LED d_7 (.in(modifying_the_alu_1_au_dout[7]));
  reg4bits reg4bits_1 (
    .DIN(controlled_buffer_1_out), .WE(we), .OE(oe), .Clock(clock_1_out), .dout(reg4bits_1_dout),
    .sd(mar_content));  // open: Reset
  reg8bits reg8bits_4 (
    .Din(modifying_the_alu_1_au_dout), .WE(we_2), .OE(oe_2), .clock(clock_1_out),
    .dout(modifying_the_alu_1_au_dout), .sd(mbr_content));  // open: Reset
  reg8bits reg8bits_5 (
    .Din(modifying_the_alu_1_au_dout), .WE(we_5), .OE(o_e), .clock(clock_1_out),
    .dout(modifying_the_alu_1_au_dout), .sd(out_31));  // open: Reset
  LED d_5 (.in(modifying_the_alu_1_au_dout[5]));
  LED d_6 (.in(modifying_the_alu_1_au_dout[6]));
  _7_Segment_Display u_7_segment_display_10 (
    .g(decimal_decoder_4_dout[15]), .f(decimal_decoder_4_dout[14]), .a(decimal_decoder_4_dout[13]),
    .b(decimal_decoder_4_dout[12]), .e(decimal_decoder_4_dout_2[3]), .d(decimal_decoder_4_dout_2[2]),
    .c(decimal_decoder_4_dout_2[1]), .dp(decimal_decoder_4_dout_2[0]));
  LED d_4 (.in(modifying_the_alu_1_au_dout[4]));
  Decimal_Decoder decimal_decoder_4 (.Din(out_31), .Dout({decimal_decoder_4_dout_2, decimal_decoder_4_dout}));
  _7_Segment_Display u_7_segment_display_11 (
    .g(decimal_decoder_4_dout[11]), .f(decimal_decoder_4_dout[10]), .a(decimal_decoder_4_dout[9]),
    .b(decimal_decoder_4_dout[8]), .e(decimal_decoder_4_dout[27]), .d(decimal_decoder_4_dout[26]),
    .c(decimal_decoder_4_dout[25]), .dp(decimal_decoder_4_dout[24]));
  _7_Segment_Display u_7_segment_display_12 (
    .g(decimal_decoder_4_dout[7]), .f(decimal_decoder_4_dout[6]), .a(decimal_decoder_4_dout[5]),
    .b(decimal_decoder_4_dout[4]), .e(decimal_decoder_4_dout[23]), .d(decimal_decoder_4_dout[22]),
    .c(decimal_decoder_4_dout[21]), .dp(decimal_decoder_4_dout[20]));
  _7_Segment_Display u_7_segment_display_13 (
    .g(decimal_decoder_4_dout[3]), .f(decimal_decoder_4_dout[2]), .a(decimal_decoder_4_dout[1]),
    .b(decimal_decoder_4_dout[0]), .e(decimal_decoder_4_dout[19]), .d(decimal_decoder_4_dout[18]),
    .c(decimal_decoder_4_dout[17]), .dp(decimal_decoder_4_dout[16]));
  LED d_3 (.in(modifying_the_alu_1_au_dout[3]));
  assign reg4bits_1_dout = in_15 ? in_11 : 4'bz;  // Controlled_Buffer controlled_buffer_4
  LED d_2 (.in(modifying_the_alu_1_au_dout[2]));
  LED d_1 (.in(modifying_the_alu_1_au_dout[1]));
  LED d_0 (.in(modifying_the_alu_1_au_dout[0]));
  RAM #(.addrWidth(4), .enables("line")) ram_1 (
    .addr(reg4bits_1_dout), .we(write_enable), .clk(clock_1_out), .din(modifying_the_alu_1_au_dout),
    .dout(ram_1_dout));
  assign modifying_the_alu_1_au_dout = in_18 ? ram_1_dout : 8'bz;  // Controlled_Buffer controlled_buffer_5
  Counter #(.max('h5), .width(3)) Step_Counter (
    .clk(clock_1_out), .Q(sc_content));  // open: clr, load, up, count, D, carry
  BitSelector #(.group(4)) bitselector_2 (.in(ir_content), .out(bitselector_2_out), .sel(1'b1));
  assign bit_extender_2_out = {{5{1'b0}}, sc_content};  // Bit_Extender bit_extender_2
  Decimal_Decoder decimal_decoder_5 (.Din(bit_extender_2_out), .Dout(out_37));
  _7_Segment_Display u_7_segment_display_14 (
    .g(out_37[3]), .f(out_37[2]), .a(out_37[1]), .b(out_37[0]), .e(out_37[19]), .d(out_37[18]),
    .c(out_37[17]), .dp(out_37[16]));
  CU Control_Unit (
    .OPC3(bitselector_2_out[3]), .OPC2(bitselector_2_out[2]), .OPC1(bitselector_2_out[1]),
    .OPC0(bitselector_2_out[0]), .SC2(sc_content[2]), .SC1(sc_content[1]), .SC0(sc_content[0]));  // open: C0, C1, C2, C3, C4, C5, C6, C7, C8, C9, C10, C11, C12, C13, C14, C15

  // Notes on the sheet:
  //   clock
  //   Instruction Register (IR)
  //   register A
  //   ALU
  //   register B
  //   controlled buffer
  //   Internal Address Bus (4 bits) 
  //   Internal Address Bus
  //   Part 1: Designing a Program Counter (PC) 
  //   Updated Datapath with Program Counter and 7-segment display features 
  //   Memory Buffer Register (MBR)
  //   Memory Address Register (MAR)
  //    Output Register (OR)
  //   controlled buffer
  //   output_reg_content
  //   External Address Bus
  //   External Address Bus
  //   oe test
  //   oe
  //   RAM
endmodule

module addsub32 (
  input  Control,
  input  [31:0] A,
  input  [31:0] B,
  output [7:0] sum_or_difference,
  output discarded_overflow
);

  wire fullbitadder_1_carry, fullbitadder_2_carry, fullbitadder_4_carry, fullbitadder_5_carry,
       fullbitadder_7_carry, fullbitadder_8_carry, fullbitadder_10_carry, fullbitadder_11_carry,
       fullbitadder_13_carry, fullbitadder_14_carry, fullbitadder_15_carry, fullbitadder_16_carry,
       fullbitadder_17_carry, fullbitadder_18_carry, fullbitadder_19_carry, fullbitadder_20_carry,
       fullbitadder_21_carry, fullbitadder_22_carry, fullbitadder_23_carry, fullbitadder_24_carry,
       fullbitadder_25_carry, fullbitadder_26_carry, fullbitadder_27_carry, fullbitadder_28_carry,
       fullbitadder_29_carry, fullbitadder_30_carry, fullbitadder_31_carry, fullbitadder_32_carry, xor_1_out,
       xor_2_out, xor_3_out, xor_4_out, xor_5_out, xor_6_out, xor_7_out, xor_8_out, xor_9_out, xor_10_out,
       xor_11_out, xor_12_out, xor_13_out, xor_14_out, xor_15_out, xor_16_out, xor_17_out, xor_18_out,
       xor_19_out, xor_20_out, xor_21_out, xor_22_out, xor_23_out, xor_24_out, xor_25_out, xor_26_out,
       xor_27_out, xor_28_out, xor_29_out, xor_30_out, xor_31_out, xor_32_out;

  // XOR_Gate xor_1 has open pins: out=xor_1_out
  // XOR_Gate xor_2 has open pins: out=xor_2_out
  // XOR_Gate xor_3 has open pins: out=xor_3_out
  // XOR_Gate xor_4 has open pins: out=xor_4_out
  // XOR_Gate xor_5 has open pins: out=xor_5_out
  // XOR_Gate xor_6 has open pins: out=xor_6_out
  // XOR_Gate xor_7 has open pins: out=xor_7_out
  // XOR_Gate xor_8 has open pins: out=xor_8_out
  // XOR_Gate xor_9 has open pins: out=xor_9_out
  // XOR_Gate xor_10 has open pins: out=xor_10_out
  // XOR_Gate xor_11 has open pins: out=xor_11_out
  // XOR_Gate xor_12 has open pins: out=xor_12_out
  // XOR_Gate xor_13 has open pins: out=xor_13_out
  // XOR_Gate xor_14 has open pins: out=xor_14_out
  // XOR_Gate xor_15 has open pins: out=xor_15_out
  // XOR_Gate xor_16 has open pins: out=xor_16_out
  // XOR_Gate xor_17 has open pins: out=xor_17_out
  // XOR_Gate xor_18 has open pins: out=xor_18_out
  // XOR_Gate xor_19 has open pins: out=xor_19_out
  // XOR_Gate xor_20 has open pins: out=xor_20_out
  // XOR_Gate xor_21 has open pins: out=xor_21_out
  // XOR_Gate xor_22 has open pins: out=xor_22_out
  // XOR_Gate xor_23 has open pins: out=xor_23_out
  // XOR_Gate xor_24 has open pins: out=xor_24_out
  xor xor_25 (xor_25_out, Control, B[24]);
  xor xor_26 (xor_26_out, Control, B[25]);
  xor xor_27 (xor_27_out, Control, B[26]);
  xor xor_28 (xor_28_out, Control, B[27]);
  xor xor_29 (xor_29_out, Control, B[28]);
  xor xor_30 (xor_30_out, Control, B[29]);
  xor xor_31 (xor_31_out, Control, B[30]);
  xor xor_32 (xor_32_out, Control, B[31]);
  fullbitadder fullbitadder_1 (
    .B(xor_8_out), .Cin(fullbitadder_13_carry), .Carry(fullbitadder_1_carry));  // open: A, Sum
  fullbitadder fullbitadder_2 (
    .B(xor_13_out), .Cin(fullbitadder_17_carry), .Carry(fullbitadder_2_carry));  // open: A, Sum
  fullbitadder fullbitadder_3 (.B(xor_14_out), .Cin(fullbitadder_2_carry));  // open: A, Sum, Carry
  fullbitadder fullbitadder_4 (
    .B(xor_1_out), .Cin(fullbitadder_18_carry), .Carry(fullbitadder_4_carry));  // open: A, Sum
  fullbitadder fullbitadder_5 (
    .B(xor_20_out), .Cin(fullbitadder_22_carry), .Carry(fullbitadder_5_carry));  // open: A, Sum
  fullbitadder fullbitadder_6 (.B(xor_2_out), .Cin(fullbitadder_5_carry));  // open: A, Sum, Carry
  fullbitadder fullbitadder_7 (
    .B(xor_4_out), .Cin(fullbitadder_23_carry), .Carry(fullbitadder_7_carry));  // open: A, Sum
  fullbitadder fullbitadder_8 (
    .B(xor_6_out), .Cin(fullbitadder_27_carry), .Carry(fullbitadder_8_carry));  // open: A, Sum
  fullbitadder fullbitadder_9 (.B(xor_24_out), .Cin(fullbitadder_8_carry));  // open: A, Sum, Carry
  fullbitadder fullbitadder_10 (
    .A(A[25]), .B(xor_26_out), .Cin(fullbitadder_28_carry), .Sum(sum_or_difference[1]),
    .Carry(fullbitadder_10_carry));
  fullbitadder fullbitadder_11 (
    .A(A[30]), .B(xor_31_out), .Cin(fullbitadder_32_carry), .Sum(sum_or_difference[6]),
    .Carry(fullbitadder_11_carry));
  fullbitadder fullbitadder_12 (
    .A(A[31]), .B(xor_32_out), .Cin(fullbitadder_11_carry), .Sum(sum_or_difference[7]),
    .Carry(discarded_overflow));
  fullbitadder fullbitadder_13 (.B(xor_7_out), .Carry(fullbitadder_13_carry));  // open: A, Cin, Sum
  fullbitadder fullbitadder_14 (
    .B(xor_9_out), .Cin(fullbitadder_1_carry), .Carry(fullbitadder_14_carry));  // open: A, Sum
  fullbitadder fullbitadder_15 (
    .B(xor_10_out), .Cin(fullbitadder_14_carry), .Carry(fullbitadder_15_carry));  // open: A, Sum
  fullbitadder fullbitadder_16 (
    .B(xor_11_out), .Cin(fullbitadder_15_carry), .Carry(fullbitadder_16_carry));  // open: A, Sum
  fullbitadder fullbitadder_17 (
    .B(xor_12_out), .Cin(fullbitadder_16_carry), .Carry(fullbitadder_17_carry));  // open: A, Sum
  fullbitadder fullbitadder_18 (.B(xor_15_out), .Carry(fullbitadder_18_carry));  // open: A, Cin, Sum
  fullbitadder fullbitadder_19 (
    .B(xor_16_out), .Cin(fullbitadder_4_carry), .Carry(fullbitadder_19_carry));  // open: A, Sum
  fullbitadder fullbitadder_20 (
    .B(xor_17_out), .Cin(fullbitadder_19_carry), .Carry(fullbitadder_20_carry));  // open: A, Sum
  fullbitadder fullbitadder_21 (
    .B(xor_18_out), .Cin(fullbitadder_20_carry), .Carry(fullbitadder_21_carry));  // open: A, Sum
  fullbitadder fullbitadder_22 (
    .B(xor_19_out), .Cin(fullbitadder_21_carry), .Carry(fullbitadder_22_carry));  // open: A, Sum
  fullbitadder fullbitadder_23 (.B(xor_3_out), .Carry(fullbitadder_23_carry));  // open: A, Cin, Sum
  fullbitadder fullbitadder_24 (
    .B(xor_21_out), .Cin(fullbitadder_7_carry), .Carry(fullbitadder_24_carry));  // open: A, Sum
  fullbitadder fullbitadder_25 (
    .B(xor_22_out), .Cin(fullbitadder_24_carry), .Carry(fullbitadder_25_carry));  // open: A, Sum
  fullbitadder fullbitadder_26 (
    .B(xor_23_out), .Cin(fullbitadder_25_carry), .Carry(fullbitadder_26_carry));  // open: A, Sum
  fullbitadder fullbitadder_27 (
    .B(xor_5_out), .Cin(fullbitadder_26_carry), .Carry(fullbitadder_27_carry));  // open: A, Sum
  fullbitadder fullbitadder_28 (
    .A(A[24]), .B(xor_25_out), .Cin(Control), .Sum(sum_or_difference[0]), .Carry(fullbitadder_28_carry));
  fullbitadder fullbitadder_29 (
    .A(A[26]), .B(xor_27_out), .Cin(fullbitadder_10_carry), .Sum(sum_or_difference[2]),
    .Carry(fullbitadder_29_carry));
  fullbitadder fullbitadder_30 (
    .A(A[27]), .B(xor_28_out), .Cin(fullbitadder_29_carry), .Sum(sum_or_difference[3]),
    .Carry(fullbitadder_30_carry));
  fullbitadder fullbitadder_31 (
    .A(A[28]), .B(xor_29_out), .Cin(fullbitadder_30_carry), .Sum(sum_or_difference[4]),
    .Carry(fullbitadder_31_carry));
  fullbitadder fullbitadder_32 (
    .A(A[29]), .B(xor_30_out), .Cin(fullbitadder_31_carry), .Sum(sum_or_difference[5]),
    .Carry(fullbitadder_32_carry));

  // Notes on the sheet:
  //   32-bit Full Adder to Perform Subtraction
endmodule

module ALU_Again (
);

  // AND_Gate and_1 is placed but not wired
  // OR_Gate or_1 is placed but not wired
  // XOR_Gate xor_1 is placed but not wired
  // Shift_Register shift_register_1: pin names not known
  // NOT_Gate not_1 is placed but not wired
  Multiplexer multiplexer_1 ();  // open: in0, in1, out, sel
  Multiplexer multiplexer_2 ();  // open: in0, in1, out, sel
endmodule

module Reg_test_file (
  input  RegWrite,
  input  clk,
  input  [31:0] BusW
);

  wire and_1_out, and_2_out, and_3_out, and_4_out, and_5_out, and_6_out, and_7_out, and_8_out, and_9_out,
       and_10_out, and_11_out, and_12_out, and_13_out, and_14_out, and_15_out, and_16_out, and_17_out,
       and_18_out, and_19_out, and_20_out, and_21_out, and_22_out, and_23_out, and_24_out, and_25_out,
       and_26_out, and_27_out, and_28_out, and_29_out, and_30_out, and_31_out, decoder_1_out1,
       decoder_1_out2, decoder_1_out3, decoder_1_out4, decoder_1_out5, decoder_1_out6, decoder_1_out7,
       decoder_1_out8, decoder_1_out9, decoder_1_out10, decoder_1_out11, decoder_1_out12, decoder_1_out13,
       decoder_1_out14, decoder_1_out15, decoder_1_out16, decoder_1_out17, decoder_1_out18, decoder_1_out19,
       decoder_1_out20, decoder_1_out21, decoder_1_out22, decoder_1_out23, decoder_1_out24, decoder_1_out25,
       decoder_1_out26, decoder_1_out27, decoder_1_out28, decoder_1_out29, decoder_1_out30, decoder_1_out31,
       undriven;

  Decoder #(.enable("false"), .select(5)) decoder_1 (
    .out1(decoder_1_out1), .out2(decoder_1_out2), .out3(decoder_1_out3), .out4(decoder_1_out4),
    .out5(decoder_1_out5), .out6(decoder_1_out6), .out7(decoder_1_out7), .out8(decoder_1_out8),
    .out9(decoder_1_out9), .out10(decoder_1_out10), .out11(decoder_1_out11), .out12(decoder_1_out12),
    .out13(decoder_1_out13), .out14(decoder_1_out14), .out15(decoder_1_out15), .out16(decoder_1_out16),
    .out17(decoder_1_out17), .out18(decoder_1_out18), .out19(decoder_1_out19), .out20(decoder_1_out20),
    .out21(decoder_1_out21), .out22(decoder_1_out22), .out23(decoder_1_out23), .out24(decoder_1_out24),
    .out25(decoder_1_out25), .out26(decoder_1_out26), .out27(decoder_1_out27), .out28(decoder_1_out28),
    .out29(decoder_1_out29), .out30(decoder_1_out30), .out31(decoder_1_out31));  // open: out0, sel
  and and_1 (and_1_out, decoder_1_out1, RegWrite);
  and and_2 (and_2_out, decoder_1_out2, RegWrite);
  and and_3 (and_3_out, decoder_1_out3, RegWrite);
  and and_4 (and_4_out, decoder_1_out4, undriven);
  and and_5 (and_5_out, decoder_1_out5, RegWrite);
  and and_6 (and_6_out, decoder_1_out6, RegWrite);
  and and_7 (and_7_out, decoder_1_out7, RegWrite);
  and and_8 (and_8_out, decoder_1_out8, RegWrite);
  and and_9 (and_9_out, decoder_1_out9, RegWrite);
  and and_10 (and_10_out, decoder_1_out10, RegWrite);
  and and_11 (and_11_out, decoder_1_out11, RegWrite);
  and and_12 (and_12_out, decoder_1_out12, RegWrite);
  and and_13 (and_13_out, decoder_1_out13, RegWrite);
  and and_14 (and_14_out, decoder_1_out14, RegWrite);
  and and_15 (and_15_out, decoder_1_out15, RegWrite);
  and and_16 (and_16_out, decoder_1_out16, RegWrite);
  and and_17 (and_17_out, decoder_1_out17, RegWrite);
  and and_18 (and_18_out, decoder_1_out18, RegWrite);
  and and_19 (and_19_out, decoder_1_out19, RegWrite);
  and and_20 (and_20_out, decoder_1_out20, RegWrite);
  and and_21 (and_21_out, decoder_1_out21, RegWrite);
  and and_22 (and_22_out, decoder_1_out22, RegWrite);
  and and_23 (and_23_out, decoder_1_out23, RegWrite);
  and and_24 (and_24_out, decoder_1_out24, RegWrite);
  and and_25 (and_25_out, decoder_1_out25, RegWrite);
  and and_26 (and_26_out, decoder_1_out26, RegWrite);
  and and_27 (and_27_out, decoder_1_out27, RegWrite);
  and and_28 (and_28_out, decoder_1_out28, RegWrite);
  and and_29 (and_29_out, decoder_1_out29, RegWrite);
  and and_30 (and_30_out, decoder_1_out30, RegWrite);
  and and_31 (and_31_out, decoder_1_out31, RegWrite);
  Register #(.width(32)) register_1 (.D(BusW), .en(and_1_out), .clk(clk));  // open: Q, clr
  Register #(.width(32)) register_2 (.D(BusW), .en(and_2_out), .clk(clk));  // open: Q, clr
  Register #(.width(32)) register_3 (.D(BusW), .en(and_3_out), .clk(clk));  // open: Q, clr
  Register #(.width(32)) register_4 (.D(BusW), .en(and_4_out), .clk(clk));  // open: Q, clr
  Register #(.width(32)) register_5 (.D(BusW), .en(and_5_out), .clk(clk));  // open: Q, clr
  Register #(.width(32)) register_6 (.D(BusW), .en(and_6_out), .clk(clk));  // open: Q, clr
  Register #(.width(32)) register_7 (.D(BusW), .en(and_7_out), .clk(clk));  // open: Q, clr
  Register #(.width(32)) register_8 (.D(BusW), .en(and_8_out), .clk(clk));  // open: Q, clr
  Register #(.width(32)) register_9 (.D(BusW), .en(and_9_out), .clk(clk));  // open: Q, clr
  Register #(.width(32)) register_10 (.D(BusW), .en(and_10_out), .clk(clk));  // open: Q, clr
  Register #(.width(32)) register_11 (.D(BusW), .en(and_11_out), .clk(clk));  // open: Q, clr
  Register #(.width(32)) register_12 (.D(BusW), .en(and_12_out), .clk(clk));  // open: Q, clr
  Register #(.width(32)) register_13 (.D(BusW), .en(and_13_out), .clk(clk));  // open: Q, clr
  Register #(.width(32)) register_14 (.D(BusW), .en(and_14_out));  // open: clk, Q, clr
  Register #(.width(32)) register_15 (.D(BusW), .en(and_15_out), .clk(clk));  // open: Q, clr
  Register #(.width(32)) register_16 (.D(BusW), .en(and_16_out), .clk(clk));  // open: Q, clr
  Register #(.width(32)) register_17 (.D(BusW), .en(and_17_out), .clk(clk));  // open: Q, clr
  Register #(.width(32)) register_18 (.D(BusW), .en(and_18_out), .clk(clk));  // open: Q, clr
  Register #(.width(32)) register_19 (.D(BusW), .en(and_19_out), .clk(clk));  // open: Q, clr
  Register #(.width(32)) register_20 (.D(BusW), .en(and_20_out), .clk(clk));  // open: Q, clr
  Register #(.width(32)) register_21 (.D(BusW), .en(and_21_out), .clk(clk));  // open: Q, clr
  Register #(.width(32)) register_22 (.D(BusW), .en(and_22_out), .clk(clk));  // open: Q, clr
  Register #(.width(32)) register_23 (.D(BusW), .en(and_23_out), .clk(clk));  // open: Q, clr
  Register #(.width(32)) register_24 (.D(BusW), .en(and_24_out), .clk(clk));  // open: Q, clr
  Register #(.width(32)) register_25 (.D(BusW), .en(and_25_out), .clk(clk));  // open: Q, clr
  Register #(.width(32)) register_26 (.D(BusW), .en(and_26_out), .clk(clk));  // open: Q, clr
  Register #(.width(32)) register_27 (.D(BusW), .en(and_27_out), .clk(clk));  // open: Q, clr
  Register #(.width(32)) register_28 (.D(BusW), .en(and_29_out), .clk(clk));  // open: Q, clr
  Register #(.width(32)) register_29 (.D(BusW), .en(and_28_out), .clk(clk));  // open: Q, clr
  Register #(.width(32)) register_30 (.D(BusW), .en(and_30_out), .clk(clk));  // open: Q, clr
  Register #(.width(32)) register_31 (.D(BusW), .en(and_31_out), .clk(clk));  // open: Q, clr
endmodule
